// Logisim project SIS.circ as structural Verilog: 1 circuit, main circuit main
module main (
  input  in_1,
  input  in_2,
  input  in_3,
  input  in_4
);

  wire and_1_out, and_2_out, and_3_out, and_4_out, and_5_out, and_6_out, and_7_out, and_8_out, and_9_out,
       and_10_out, and_11_out, and_12_out, and_13_out, and_14_out, and_15_out, and_16_out, and_17_out,
       and_18_out, and_19_out, and_20_out, and_21_out, and_22_out, and_23_out, and_24_out, and_25_out,
       and_26_out, and_27_out, and_28_out, and_29_out, and_30_out, and_31_out, and_32_out, and_33_out,
       and_34_out, and_35_out, and_36_out, nand_1_out, nand_2_out, nand_3_out, nand_4_out, nand_5_out,
       nor_1_out, nor_2_out, nor_3_out, nor_4_out, not_1_out, not_2_out, not_3_out, not_4_out, not_5_out,
       not_6_out, not_7_out, not_8_out, not_9_out, not_10_out, not_11_out, not_12_out, not_13_out,
       not_14_out, not_15_out, not_16_out, not_17_out, not_18_out, not_19_out, not_20_out, not_21_out,
       not_22_out, not_23_out, not_24_out, not_25_out, not_26_out, not_27_out, not_28_out, not_29_out,
       not_30_out, not_31_out, not_32_out, not_33_out, not_34_out, not_35_out, not_36_out, not_37_out,
       not_38_out, not_39_out, or_1_out, or_2_out, or_3_out, or_4_out, or_5_out, or_6_out, or_7_out,
       or_8_out, or_9_out, or_10_out, or_11_out, or_12_out, or_13_out, or_14_out, or_15_out, or_16_out,
       or_17_out, or_18_out, or_19_out, or_20_out, or_21_out, or_22_out, or_23_out, or_24_out, or_25_out,
       or_26_out, or_27_out, or_28_out, or_29_out, or_30_out, or_31_out, or_32_out, or_33_out, or_34_out,
       xor_1_out, xor_2_out;

  not not_1 (not_1_out, in_1);
  not not_2 (not_2_out, in_2);
  not not_3 (not_3_out, in_2);
  not not_4 (not_4_out, in_2);
  not not_5 (not_5_out, in_2);
  not not_6 (not_6_out, in_1);
  nor nor_1 (nor_1_out, in_3, in_4);
  not not_7 (not_7_out, in_4);
  not not_8 (not_8_out, in_1);
  not not_9 (not_9_out, in_4);
  not not_10 (not_10_out, in_4);
  not not_11 (not_11_out, in_4);
  or or_1 (or_1_out, in_3, in_4);
  nor nor_2 (nor_2_out, in_3, in_4);
  not not_12 (not_12_out, in_2);
  and and_1 (and_1_out, in_3, in_4);
  not not_13 (not_13_out, in_1);
  not not_14 (not_14_out, in_2);
  or or_2 (or_2_out, in_3, in_4);
  not not_15 (not_15_out, in_4);
  not not_16 (not_16_out, in_2);
  not not_17 (not_17_out, in_1);
  not not_18 (not_18_out, in_4);
  not not_19 (not_19_out, in_2);
  not not_20 (not_20_out, in_4);
  not not_21 (not_21_out, in_1);
  nand nand_1 (nand_1_out, in_3, in_4);
  not not_22 (not_22_out, in_2);
  not not_23 (not_23_out, in_3);
  not not_24 (not_24_out, in_4);
  not not_25 (not_25_out, in_2);
  not not_26 (not_26_out, in_4);
  not not_27 (not_27_out, in_1);
  nor nor_3 (nor_3_out, in_3, in_4);
  not not_28 (not_28_out, in_2);
  and and_2 (and_2_out, in_3, in_4);
  not not_29 (not_29_out, in_4);
  not not_30 (not_30_out, in_2);
  xor xor_1 (xor_1_out, in_3, in_4);
  not not_31 (not_31_out, in_1);
  not not_32 (not_32_out, in_4);
  not not_33 (not_33_out, in_2);
  not not_34 (not_34_out, in_4);
  not not_35 (not_35_out, in_4);
  not not_36 (not_36_out, in_2);
  not not_37 (not_37_out, in_4);
  not not_38 (not_38_out, in_1);
  or or_3 (or_3_out, in_3, in_4);
  not not_39 (not_39_out, in_2);
  and and_3 (and_3_out, not_1_out, not_2_out);
  or or_4 (or_4_out, not_3_out, in_2);
  or or_5 (or_5_out, not_5_out, in_1);
  or or_6 (or_6_out, not_6_out, in_2);
  or or_7 (or_7_out, in_3, not_7_out);
  or or_8 (or_8_out, not_8_out, in_2);
  or or_9 (or_9_out, or_8_out, in_1);
  or or_10 (or_10_out, in_3, not_10_out);
  nand nand_2 (nand_2_out, in_3, not_11_out);
  and and_4 (and_4_out, or_1_out, in_2);
  and and_5 (and_5_out, nor_2_out, not_12_out);
  and and_6 (and_6_out, in_2, and_1_out);
  and and_7 (and_7_out, in_3, not_14_out);
  and and_8 (and_8_out, in_2, or_2_out);
  or or_11 (or_11_out, in_3, not_15_out);
  and and_9 (and_9_out, or_11_out, not_16_out);
  and and_10 (and_10_out, in_2, xor_2_out);
  xor xor_2 (xor_2_out, in_3, in_4);
  nand nand_3 (nand_3_out, in_3, not_18_out);
  and and_11 (and_11_out, nand_3_out, not_19_out);
  and and_12 (and_12_out, in_2, or_12_out);
  or or_12 (or_12_out, in_3, not_20_out);
  and and_13 (and_13_out, nand_1_out, not_22_out);
  and and_14 (and_14_out, in_2, not_23_out);
  and and_15 (and_15_out, not_24_out, not_25_out);
  and and_16 (and_16_out, in_2, nor_4_out);
  nor nor_4 (nor_4_out, in_3, not_26_out);
  and and_17 (and_17_out, nor_3_out, not_28_out);
  and and_18 (and_18_out, in_2, and_2_out);
  or or_13 (or_13_out, in_3, not_29_out);
  and and_19 (and_19_out, or_13_out, not_30_out);
  and and_20 (and_20_out, in_2, xor_1_out);
  nand nand_4 (nand_4_out, in_3, in_3, not_32_out);
  and and_21 (and_21_out, nand_4_out, not_33_out);
  and and_22 (and_22_out, in_2, or_14_out);
  or or_14 (or_14_out, in_3, not_34_out);
  nand nand_5 (nand_5_out, in_3, not_35_out);
  and and_23 (and_23_out, nand_5_out, not_36_out);
  and and_24 (and_24_out, in_2, or_15_out);
  or or_15 (or_15_out, in_3, not_37_out);
  and and_25 (and_25_out, or_3_out, not_39_out);
  _7_Segment_Display u_7_segment_display_1 (
    .g(in_1), .f(and_3_out), .a(or_16_out), .b(or_4_out), .e(not_4_out), .d(or_5_out), .c(or_6_out));  // open: dp
  or or_16 (or_16_out, and_3_out, in_1);
  or or_17 (or_17_out, in_3, and_4_out, in_1);
  or or_18 (or_18_out, and_5_out, and_6_out);
  or or_19 (or_19_out, and_7_out, and_8_out);
  or or_20 (or_20_out, and_9_out, and_10_out);
  or or_21 (or_21_out, and_11_out, and_12_out);
  and and_26 (and_26_out, in_1, or_22_out);
  or or_22 (or_22_out, and_13_out, and_14_out);
  or or_23 (or_23_out, and_15_out, and_16_out);
  or or_24 (or_24_out, and_17_out, and_18_out);
  or or_25 (or_25_out, and_19_out, and_20_out);
  or or_26 (or_26_out, and_21_out, and_22_out);
  or or_27 (or_27_out, and_23_out, and_24_out);
  or or_28 (or_28_out, and_25_out, in_2);
  _7_Segment_Display u_7_segment_display_2 (
    .g(in_3), .f(nor_1_out), .a(or_7_out), .b(or_9_out), .e(not_9_out), .d(or_10_out), .c(nand_2_out));  // open: dp
  and and_27 (and_27_out, or_18_out, not_13_out);
  or or_29 (or_29_out, and_27_out, and_28_out);
  and and_28 (and_28_out, or_19_out, in_1);
  and and_29 (and_29_out, or_20_out, not_17_out);
  and and_30 (and_30_out, in_1, or_21_out);
  or or_30 (or_30_out, not_21_out, and_26_out);
  and and_31 (and_31_out, or_23_out, not_27_out);
  and and_32 (and_32_out, in_1, or_24_out);
  and and_33 (and_33_out, or_25_out, not_31_out);
  and and_34 (and_34_out, in_1, or_26_out);
  and and_35 (and_35_out, or_27_out, not_38_out);
  and and_36 (and_36_out, in_1, or_28_out, or_28_out);
  _7_Segment_Display u_7_segment_display_3 (
    .g(or_17_out), .f(or_29_out), .a(or_31_out), .b(or_30_out), .e(or_32_out), .d(or_33_out), .c(or_34_out));  // open: dp
  or or_31 (or_31_out, and_29_out, and_30_out);
  or or_32 (or_32_out, and_31_out, and_32_out);
  or or_33 (or_33_out, and_33_out, and_34_out);
  or or_34 (or_34_out, and_35_out, and_36_out);
endmodule
